# Fritzing sketch Milestone Pico Pinout (saved by Fritzing 0.9.10b)
breadboards: 1

parts:
  Pico_H1 = Raspberry Pi Pico H  # not connected
  U1 = Nokia 6100 Color LCD [package=nokia6100_lcd]  # not connected
  M1 = Dagu DGServo 9g (Top view) [part_number=RS001B]
  M2 = Dagu DGServo 9g (Top view) [part_number=RS001B]
  M3 = Dagu DGServo 9g (Top view) [part_number=RS001B]
  M4 = Dagu DGServo 9g (Top view) [part_number=RS001B]
  LED1 = RGB LED - (4 legs) [package="5 mm [THT]"]
  LED2 = RGB LED - (4 legs) [package="5 mm [THT]"]
  LED3 = LED - 5mm [color="Red (633nm)" current=0.030 package="5 mm [THT]"]
  LED4 = LED - 5mm [color="Red (633nm)" current=0.030 package="5 mm [THT]"]
  LED5 = LED - 5mm [color="Red (633nm)" current=0.030 package="5 mm [THT]"]
  R1 = Resistor [tolerance=±5% resistance=220 package="1206 [SMD]"]
  R2 = Resistor [tolerance=±5% resistance=220 package="0603 [SMD]"]
  R3 = Resistor [tolerance=±5% resistance=220 package="0603 [SMD]"]
  R4 = Resistor [tolerance=±5% resistance=220 package="0603 [SMD]"]
  R5 = Resistor [tolerance=±5% resistance=220 package="0603 [SMD]"]
  R6 = Resistor [tolerance=±5% resistance=220 package="0603 [SMD]"]
  R7 = Resistor [tolerance=±5% resistance=220 package="0603 [SMD]"]
  R8 = Resistor [tolerance=±5% resistance=220 package="0603 [SMD]"]
  R9 = Resistor [tolerance=±5% resistance=220 package="0603 [SMD]"]

nets:
  GND: M1.gnd, M2.gnd, M3.gnd, M4.gnd
  VCC: M1.vcc, M2.vcc, M3.vcc, M4.vcc
  N1: LED1.red_cathode, R3.Pin_1
  N2: LED1.common_anode, LED2.common_anode, LED3.cathode, LED4.cathode, LED5.cathode
  N3: LED1.green_cathode, R1.Pin_1
  N4: LED1.blue_cathode, R2.Pin_1
  N5: LED2.red_cathode, R4.Pin_1
  N6: LED2.green_cathode, R5.Pin_1
  N7: LED2.blue_cathode, R6.Pin_1
  N8: LED3.anode, R7.Pin_1
  N9: LED4.anode, R8.Pin_1
  N10: LED5.anode, R9.Pin_1

notes:
  Servo:
  - Left foot lower: GP21
  - Right foot lower: GP20
  - Left foot upper: GP19
  - Right foot upper: GP18
  LCD:
  - DC (Data command): GP8
  - CS (chip select): GP9
  - CLK (SPI clock): GP10
  - DIN (Master out, slave in): GP11
  - RST (Active low reset): GP12
  - BL (backlight): GP13
  Example display, not the actual model we are using (need to find the model and import to Fritizing)
  Off Board Wireless Hardware
  - The robot can be wirelessly controlled via 3 different nodes
  1. There is a second Pico MCU with a keypad connected directly to the pins. This Pico is connected then connected to a laptop that parses serial input from the Pico/keypad. This allows the keypad to act as a remote robot controller
  2. There is also another laptop running a Flask server to wirelessly control the robot
  3. There is also a mobile device connected to the same Flask server to wirelessly control the robot

custom parts:
  Raspberry Pi Pico H: Raspberry Pi Pico H. Based around the RP2040 microcontroller the Pico H is a low cost microcontroller device bringing Raspberry Pi quality, cost, and easy of use to the microcontroller space.
